# Fritzing sketch circuit (saved by Fritzing 0.9.3b)
breadboards: 2

parts:
  パーツ1 = Arduino Uno (Rev3)
  J2 = Piezo Speaker
  J3 = Piezo Speaker  # not connected
  J4 = Piezo Speaker  # not connected
  R1 = Resistor [tolerance=±5% resistance=1M package="1206 [SMD]"]
  R2 = Resistor [tolerance=±5% resistance=1M package="1206 [SMD]"]
  R3 = Resistor [tolerance=±5% resistance=1M package="1206 [SMD]"]
  R4 = Resistor [tolerance=±5% resistance=1M package="1206 [SMD]"]
  U1 = DIODE-ZENER [package=diode-zener]
  U2 = DIODE-ZENER [package=diode-zener]
  U3 = DIODE-ZENER [package=diode-zener]
  U4 = DIODE-ZENER [package=diode-zener]
  S1 = Momentary Switch [package=ksa_sealed_tac_switch]
  S2 = Momentary Switch [package=ksa_sealed_tac_switch]
  S3 = Momentary Switch [package=ksa_sealed_tac_switch]
  S4 = Momentary Switch [package=ksa_sealed_tac_switch]
  LCD1 = LCD screen
  J5 = Basic Force Sensing Resistor (FSR) [package=THT]  # not connected
  S6 = Toggle Switch [package=THT]  # not connected
  S5 = Momentary Switch [package=ksa_sealed_tac_switch]
  R5 = Resistor [tolerance=±5% resistance=10k package="1206 [SMD]"]
  R6 = Resistor [tolerance=±5% resistance=10k package="1206 [SMD]"]
  U6 = 2.5mm Audio Jack [package=stereojack2.5mm_stereojack2.5mm]
  U5 = 2.5mm Audio Jack [package=stereojack2.5mm_stereojack2.5mm]
  U7 = 2.5mm Audio Jack [package=stereojack2.5mm_stereojack2.5mm]
  U8 = 2.5mm Audio Jack [package=stereojack2.5mm_stereojack2.5mm]
  J6 = Piezo Speaker

nets:
  N1: パーツ1.A0, R1.Pin_0, U1.C, U5.LEFT
  N2: パーツ1.A1, R2.Pin_0, U2.C, U5.RIGHT
  N3: パーツ1.A2, R3.Pin_0, U3.C, U6.LEFT
  N4: パーツ1.A3, R4.Pin_0, U4.C, U7.LEFT
  N5: パーツ1.A4/SDA, R5.Pin_1, U8.SLEEVE
  N6: パーツ1.D8, S3.1, S3.2
  N7: パーツ1.D9_PWM, S2.1
  N8: パーツ1.D10_PWM/SS, S1.1
  N9: パーツ1.D11_PWM/MOSI, LCD1.E
  N10: パーツ1.D12/MISO, LCD1.RS
  GND: パーツ1.GND, R1.Pin_1, R2.Pin_1, R3.Pin_1, R4.Pin_1, S1.3, S2.3, S3.3, S3.4, S4.3, S4.4, LCD1.VSS, LCD1.R/W, S5.3, R5.Pin_0, R6.Pin_0, U6.SLEEVE, U5.SLEEVE, U7.SLEEVE
  N11: パーツ1.D2, LCD1.DB7
  N12: パーツ1.D3_PWM, LCD1.DB6
  N13: パーツ1.D4, LCD1.DB5
  N14: パーツ1.D5_PWM, LCD1.DB4
  N15: パーツ1.D6_PWM, S5.1
  N16: パーツ1.D7, S4.1, S4.2
  5V: パーツ1.5V, LCD1.VDD, U8.LEFT
  N17: J2.pin1, J6.pin1
  N18: LCD1.V0, R6.Pin_1
