# Fritzing sketch button (saved by Fritzing 0.9.4)
breadboards: 1

parts:
  パーツ1 = Arduino Uno (Rev3)
  R1 = Resistor [tolerance=±5% resistance=1k package=THT]
  R2 = Resistor [tolerance=±5% resistance=1M package=THT]
  R3 = Resistor [tolerance=±5% resistance=22k package=THT]  # not connected
  パーツ2 = LCD Keypad Shield  # not connected
  S1 = Pushbutton [package=THT]
  S3 = Pushbutton [package=THT]
  S4 = Pushbutton [package=THT]
  S2 = Pushbutton [package=THT]
  S5 = Pushbutton [package=THT]

nets:
  N1: パーツ1.D8, S3.leg1
  N2: パーツ1.D9_PWM, S2.leg1
  N3: パーツ1.D10_PWM/SS, S1.leg1
  N4: パーツ1.D6_PWM, S5.leg1
  N5: パーツ1.D7, S4.leg1
  N6: パーツ1.GND, S1.leg0, S3.leg0, S4.leg0, S2.leg0, S5.leg0
  N7: R1.Pin_1, R2.Pin_0

custom parts:
  LCD Keypad Shield: It consists of a 1602 white character blue backlight LCD. The keypad consists of 5 keys — select, up, right, down and left. To save the digital IO pins, the keypad interface uses only one ADC channel. The key value is read through a 5 stage voltage divider.
