# Fritzing sketch cymbal (saved by Fritzing 0.9.4)
breadboards: 1

parts:
  パーツ1 = Arduino Uno (Rev3)
  R1 = Resistor [tolerance=±5% resistance=1k package=THT]
  R2 = Resistor [tolerance=±5% resistance=100k package=THT]
  R3 = Resistor [tolerance=±5% resistance=22k package=THT]
  R4 = Resistor [tolerance=±5% resistance=100k package=THT]

nets:
  N1: パーツ1.A0, R2.Pin_1, R4.Pin_0
  N2: パーツ1.A1, R1.Pin_0
  N3: パーツ1.5V, R3.Pin_0
  N4: パーツ1.GND, R1.Pin_1, R2.Pin_0
