# Fritzing sketch dualpiezo (saved by Fritzing 0.9.4)
breadboards: 1

parts:
  パーツ1 = Arduino Uno (Rev3)
  R1 = Resistor [tolerance=±5% resistance=100k package=THT]
  R9 = Resistor [tolerance=±5% resistance=100k package=THT]
  R11 = Resistor [tolerance=±5% resistance=100k package=THT]
  R15 = Resistor [tolerance=±5% resistance=100k package=THT]

nets:
  N1: パーツ1.A0, R1.Pin_0, R15.Pin_0
  N2: パーツ1.A1, R9.Pin_1, R11.Pin_0
  N3: パーツ1.GND, R1.Pin_1, R9.Pin_0
