# Fritzing sketch pd-8 (saved by Fritzing 0.9.4)
breadboards: 1

parts:
  パーツ1 = Arduino Uno (Rev3)
  R1 = Resistor [tolerance=±5% resistance=1k package=THT]
  R2 = Resistor [tolerance=±5% resistance=1M package=THT]
  R3 = Resistor [tolerance=±5% resistance=22k package=THT]
  R4 = Resistor [tolerance=±5% resistance=47 package=THT]
  R6 = Trimmer Potentiometer [maximum_resistance=200kΩ package=THT]
  R7 = Resistor [tolerance=±5% resistance=10k package=THT]

nets:
  N1: パーツ1.A0, R2.Pin_1, R6.wiper
  N2: パーツ1.A1, R1.Pin_0
  N3: パーツ1.5V, R3.Pin_0
  N4: パーツ1.GND, R1.Pin_1, R2.Pin_0, R7.Pin_0
  N5: R4.Pin_0, R6.leg2
  N6: R6.leg1, R7.Pin_1
