# Fritzing sketch piezo (saved by Fritzing 0.9.4)
breadboards: 1

parts:
  パーツ1 = Arduino Uno (Rev3)
  R1 = Resistor [tolerance=±5% resistance=1M package=THT]
  R2 = Resistor [tolerance=±5% resistance=1M package=THT]

nets:
  N1: パーツ1.A0, R2.Pin_0
  N2: パーツ1.A1, R1.Pin_1
  N3: パーツ1.GND, R1.Pin_0, R2.Pin_1
