# Fritzing sketch singlePiezo (saved by Fritzing 0.9.4)
breadboards: 1

parts:
  パーツ1 = Arduino Uno (Rev3)
  R14 = Resistor [tolerance=±5% resistance=100k package=THT]
  R15 = Resistor [tolerance=±5% resistance=100k package=THT]

nets:
  N1: パーツ1.A0, R14.Pin_0, R15.Pin_1
  N2: パーツ1.GND, R15.Pin_0
