# Fritzing sketch singlePiezoVariable (saved by Fritzing 0.9.4)
breadboards: 1

parts:
  パーツ1 = Arduino Uno (Rev3)
  R14 = Resistor [tolerance=±5% resistance=51k package=THT]
  R15 = Resistor [tolerance=±5% resistance=10k package=THT]
  R16 = Trimmer Potentiometer [maximum_resistance=200kΩ package=THT]

nets:
  N1: パーツ1.A0, R16.wiper
  N2: パーツ1.GND, R15.Pin_0
  N3: R14.Pin_0, R16.leg2
  N4: R15.Pin_1, R16.leg1
