# Fritzing sketch tcrt (saved by Fritzing 0.9.4)
breadboards: 2

parts:
  パーツ1 = Arduino Uno (Rev3)
  R1 = Resistor [tolerance=±5% resistance=4.7k package=THT]
  R2 = Resistor [tolerance=±5% resistance=330 package=THT]
  R3 = Resistor [tolerance=±5% resistance=10k package=THT]

nets:
  N1: パーツ1.A0, R1.Pin_1, R3.Pin_0
  N2: パーツ1.GND, R1.Pin_0, R2.Pin_1, R3.Pin_1
